# Fritzing sketch piranha-plant (saved by Fritzing 0.9.3b)
breadboards: 1

parts:
  WeMos_D1_Mini2 = WeMos D1 Mini  # not connected
  M1 = Stepper Motor - Bipolar
  Q1 = Basic FET N-Channel [package="TO220 [THT]"]
  S1 = Round Pushbutton
  Pololu_A1 = Pololu A4988 [package=SO16]
  Power_plug1 = Power plug
  LM1 = RioRand LM2596
  X1 = USB Connectors [package=usb-a-s-nosilk]
  R1 = Resistor [tolerance=±5% resistance=10k package="1206 [SMD]"]
  R2 = Resistor [tolerance=±5% resistance=10k package="1206 [SMD]"]

nets:
  N1: M1.A, Pololu_A1.SLEEP
  N2: M1.C, Pololu_A1.RESET
  N3: M1.B, Pololu_A1.MS3
  N4: M1.D, Pololu_A1.MS2
  N5: Q1.gate, R2.Pin_0
  N6: Q1.drain, X1.VBUS
  N7: Q1.source, S1.leg1, Pololu_A1.ENABLE, LM1.Pin_3, R2.Pin_1
  N8: S1.leg0, R1.Pin_0
  N9: Pololu_A1.MS1, R1.Pin_1
  N10: Pololu_A1.STEP, Power_plug1.VCC
